// Digital circuit 4bit_ALU.dlogic.dig as structural Verilog
module _4bit_ALU_dlogic (
  input  [3:0] A,
  input  [3:0] B,
  input  [2:0] Control,
  input  zero,
  output [3:0] Result,
  output Zero_Flag,
  output overflow,
  output Less_Than_Flag,
  output underflow
);

  wire _4bit_setlessthanflag_1_p4, not_1_out;
  wire [3:0] _4bit_full_adder_1_p4, _4bit_logicoperations_1_p3, _4bit_logicoperations_1_p4,
       _4bit_logicoperations_1_p5, _4bit_subtractor_1_p4;

  not not_1 (not_1_out, zero);
  // _4bit_full_adder _4bit_full_adder_1: pin names not known; wires that end beside it: zero, A, B, _4bit_full_adder_1_p4, overflow
  // _4bit_subtractor _4bit_subtractor_1: pin names not known; wires that end beside it: A, B, not_1_out, _4bit_subtractor_1_p4, underflow
  // _4bit_logicOperations _4bit_logicoperations_1: pin names not known; wires that end beside it: A, B, _4bit_logicoperations_1_p3, _4bit_logicoperations_1_p4, _4bit_logicoperations_1_p5
  // _4bit_setLessThanFlag _4bit_setlessthanflag_1: pin names not known; wires that end beside it: A, B, zero, _4bit_setlessthanflag_1_p4
  _4bit_multiplexer_6x2 _4bit_multiplexer_6x2_1 (
    .Control(Control), .ADD(_4bit_full_adder_1_p4), .SUB(_4bit_subtractor_1_p4),
    .AND(_4bit_logicoperations_1_p3), .OR(_4bit_logicoperations_1_p4), .XOR(_4bit_logicoperations_1_p5),
    .SLT(_4bit_setlessthanflag_1_p4), .R(Result), .LT(Less_Than_Flag));
  // _4bit_zeroflag _4bit_zeroflag_1: pin names not known; wires that end beside it: Result, Zero_Flag
endmodule
