// Digital circuit 4bit_setLessThanFlag.dig as structural Verilog
module _4bit_setLessThanFlag (
  input  [3:0] A,
  input  [3:0] B,
  output SLT_flag
);

  wire and_2_out, and_3_out, and_5_out, and_6_out, and_8_out, and_9_out, and_10_out, not_1_out, not_2_out,
       not_3_out, not_4_out;

  not not_1 (not_1_out, A[0]);
  and and_1 (SLT_flag, not_1_out, B[0]);
  not not_2 (not_2_out, A[1]);
  and and_2 (and_2_out, A[0], B[0]);
  and and_3 (and_3_out, not_2_out, B[1]);
  and and_4 (SLT_flag, and_2_out, and_3_out);
  and and_5 (and_5_out, A[0], B[0], A[1], B[1]);
  not not_3 (not_3_out, A[2]);
  and and_6 (and_6_out, not_3_out, B[2]);
  and and_7 (SLT_flag, and_5_out, and_6_out);
  and and_8 (and_8_out, A[0], B[0], A[1], A[1]);
  and and_9 (and_9_out, A[2], B[2]);
  not not_4 (not_4_out, A[3]);
  and and_10 (and_10_out, not_4_out, B[3]);
  and and_11 (SLT_flag, and_8_out, and_9_out, and_10_out);
endmodule
